// Digital circuit CPU.dig as structural Verilog
module CPU (
  input  [7:0] Input,
  input  _10Hz,
  input  BallsToTheWall,
  input  Hold,
  output [7:0] Output
);

  wire and_1_out, and_2_out, and_3_out, and_4_out, and_5_out, and_6_out, and_7_out, and_8_out, and_9_out,
       and_10_out, and_11_out, and_12_out, and_13_out, and_14_out, and_15_out, and_16_out, and_17_out,
       and_18_out, and_19_out, and_20_out, and_21_out, and_22_out, and_23_out, and_24_out, and_25_out,
       and_26_out, and_27_out, and_28_out, and_29_out, and_30_out, and_31_out, and_32_out, and_33_out,
       and_34_out, and_35_out, and_36_out, and_37_out, and_38_out, and_39_out, and_40_out, and_41_out,
       and_42_out, and_43_out, and_44_out, and_45_out, and_46_out, and_47_out, and_48_out, and_49_out,
       and_50_out, and_51_out, Clk, comparator_1_eq, comparator_2_eq, delay_1_out, director_1_dn,
       director_1_up, director_2_dn, director_2_up, jk_ff_1_q, jk_ff_2_q, jk_ff_3_q, jk_ff_4_q, jk_ff_5_nq,
       jk_ff_5_q, jk_ff_6_q, nClk, not_3_out, not_5_out, not_6_out, not_8_out, not_9_out, not_10_out,
       not_11_out, not_12_out, not_13_out, not_14_out, nRst, nStep_Rst, or_1_out, or_2_out, or_3_out,
       or_4_out, or_5_out, or_6_out, or_7_out, or_8_out, or_9_out, or_10_out, or_11_out, or_12_out,
       or_13_out, or_14_out, Proceed, Pulse_out, Rst, Send_out, xor_1_out;
  wire [1:0] dipswitch_1_out;
  wire [7:0] counter8_1_out, Data_d, driver_1_out, not_4_out, rom_1_d;
  wire [15:0] counter16_1_out, counter16_2_out, ProgAddr, register_1_q;

  not not_1 (nClk, Clk);
  and and_1 (and_1_out, Proceed, nClk);
  and and_2 (and_2_out, nStep_Rst, nRst);
  Button Pulse (.out(Pulse_out));
  DipSwitch dipswitch_1 (.out(dipswitch_1_out[1]));
  DipSwitch dipswitch_2 (.out(dipswitch_1_out[0]));
  or or_1 (or_1_out, jk_ff_4_q, not_3_out);
  and and_3 (and_3_out, and_2_out, or_1_out);
  not not_2 (Rst, nRst);
  DipSwitch #(.dipDefault("true")) nReset (.out(nRst));
  Multiplexer #(.Selector_Bits(2)) multiplexer_1 (
    .sel(dipswitch_1_out), .in_0(Pulse_out), .in_1(Hold), .in_2(_10Hz), .in_3(BallsToTheWall), .out(Clk));
  not not_3 (not_3_out, and_5_out);
  JK_FF jk_ff_1 (.J(and_3_out), .C(and_1_out), .K(or_3_out), .Q(jk_ff_1_q));  // open: nQ
  or or_2 (or_2_out, jk_ff_1_q, and_5_out);
  and and_4 (and_4_out, and_2_out, jk_ff_1_q);
  or or_3 (or_3_out, and_2_out, jk_ff_1_q);
  LED led_1 (.in(jk_ff_1_q));
  and and_5 (and_5_out, and_2_out, or_2_out);
  JK_FF jk_ff_2 (.J(and_4_out), .C(and_1_out), .K(or_4_out), .Q(jk_ff_2_q));  // open: nQ
  or or_4 (or_4_out, and_2_out, jk_ff_2_q);
  and and_6 (and_6_out, and_2_out, jk_ff_2_q);
  LED led_2 (.in(jk_ff_2_q));
  JK_FF jk_ff_3 (.J(and_6_out), .C(and_1_out), .K(or_5_out), .Q(jk_ff_3_q));  // open: nQ
  and and_7 (and_7_out, and_2_out, jk_ff_3_q);
  or or_5 (or_5_out, and_2_out, jk_ff_3_q);
  LED led_3 (.in(jk_ff_3_q));
  JK_FF jk_ff_4 (.J(and_7_out), .C(and_1_out), .K(or_6_out), .Q(jk_ff_4_q));  // open: nQ
  or or_6 (or_6_out, and_2_out, jk_ff_4_q);
  LED led_4 (.in(jk_ff_4_q));
  ROM #(.AddrBits(16), .Bits(8)) rom_1 (.A(ProgAddr), .sel(1'b1), .D(rom_1_d));
  assign not_4_out = ~rom_1_d;  // Not not_4, 8 bits wide
  and and_8 (and_8_out, rom_1_d[0], rom_1_d[1], not_4_out[2], rom_1_d[3]);
  and and_9 (and_9_out, rom_1_d[0], not_4_out[1], rom_1_d[2], rom_1_d[3]);
  and and_10 (and_10_out, not_4_out[4], rom_1_d[5], not_4_out[6], not_4_out[7]);
  and and_11 (and_11_out, not_4_out[0], not_4_out[1], rom_1_d[2], rom_1_d[3]);
  and and_12 (and_12_out, not_4_out[0], rom_1_d[1], rom_1_d[2], rom_1_d[3]);
  and and_13 (and_13_out, rom_1_d[4], rom_1_d[5], not_4_out[6], not_4_out[7]);
  and and_14 (and_14_out, rom_1_d[4], not_4_out[5], rom_1_d[6], not_4_out[7]);
  and and_15 (and_15_out, and_8_out, and_10_out);
  and and_16 (and_16_out, and_9_out, and_10_out);
  and and_17 (and_17_out, and_11_out, and_10_out);
  and and_18 (and_18_out, and_12_out, and_10_out);
  and and_19 (and_19_out, and_11_out, and_13_out);
  and and_20 (and_20_out, and_12_out, and_13_out);
  and and_21 (and_21_out, and_8_out, and_14_out);
  and and_22 (and_22_out, and_9_out, and_14_out);
  LED led_5 (.in(and_15_out));
  LED led_6 (.in(and_16_out));
  LED led_7 (.in(and_17_out));
  LED led_8 (.in(and_18_out));
  LED led_9 (.in(and_19_out));
  LED led_10 (.in(and_20_out));
  and and_23 (and_23_out, jk_ff_1_q, jk_ff_5_nq);
  LED led_11 (.in(and_21_out));
  LED led_12 (.in(and_22_out));
  and and_24 (and_24_out, jk_ff_2_q, jk_ff_5_nq);
  or or_7 (or_7_out, and_18_out, and_13_out);
  and and_25 (and_25_out, jk_ff_3_q, jk_ff_5_nq);
  and and_26 (and_26_out, and_24_out, and_15_out);
  and and_27 (and_27_out, and_24_out, and_16_out);
  or or_8 (or_8_out, and_15_out, and_16_out);
  and and_28 (and_28_out, and_24_out, or_7_out);
  and and_29 (and_29_out, jk_ff_4_q, jk_ff_5_nq);
  and and_30 (and_30_out, and_29_out, or_8_out);
  or or_9 (or_9_out, or_8_out, and_18_out);
  and and_31 (and_31_out, or_8_out, and_25_out);
  and and_32 (and_32_out, and_24_out, and_17_out);
  and and_33 (and_33_out, and_23_out, and_17_out);
  and and_34 (and_34_out, and_23_out, and_18_out);
  and and_35 (and_35_out, and_17_out, and_25_out);
  and and_36 (and_36_out, and_23_out, and_19_out);
  and and_37 (and_37_out, and_23_out, and_20_out);
  and and_38 (and_38_out, or_8_out, and_23_out);
  and and_39 (and_39_out, or_9_out, and_23_out);
  or or_10 (or_10_out, and_31_out, and_32_out);
  or or_11 (or_11_out, and_35_out, and_28_out);
  or or_12 (or_12_out, and_30_out, or_11_out);
  Comparator #(.Bits(8)) comparator_1 (.a(Data_d), .b({8{1'b0}}), .eq(comparator_1_eq));  // open: gt, lt
  and and_40 (and_40_out, and_14_out, jk_ff_2_q);
  and and_41 (and_41_out, and_14_out, jk_ff_1_q);
  xor xor_1 (xor_1_out, and_22_out, jk_ff_6_q);
  and and_42 (and_42_out, comparator_1_eq, and_21_out);
  not not_5 (not_5_out, comparator_1_eq);
  or or_13 (or_13_out, and_42_out, and_43_out);
  and and_43 (and_43_out, not_5_out, and_22_out);
  Director director_1 (.En(and_40_out), .Clk(nClk), .Dir(xor_1_out), .Up(director_1_up), .Dn(director_1_dn));
  LED led_13 (.in(or_13_out));
  Counter16 counter16_1 (
    .nUp(director_1_up), .nDn(director_1_dn), .In({16{1'b0}}), .nLd(1'b1), .Clr(Rst), .Out(counter16_1_out));  // open: nBO
  LED led_14 (.in(or_12_out));
  LED led_15 (.in(and_36_out));
  LED led_16 (.in(and_37_out));
  LED led_17 (.in(or_10_out));
  LED led_18 (.in(and_39_out));
  LED led_19 (.in(and_26_out));
  LED led_20 (.in(and_27_out));
  LED led_21 (.in(and_38_out));
  LED led_22 (.in(and_31_out));
  LED led_23 (.in(and_32_out));
  LED led_24 (.in(and_33_out));
  LED led_25 (.in(and_34_out));
  LED led_26 (.in(or_11_out));
  and and_44 (and_44_out, jk_ff_2_q, and_46_out);
  and and_45 (and_45_out, jk_ff_1_q, and_22_out);
  and and_46 (and_46_out, comparator_2_eq, not_8_out);
  or or_14 (or_14_out, or_12_out, and_50_out);
  not not_6 (not_6_out, and_37_out);
  not not_7 (nStep_Rst, or_11_out);
  and and_47 (and_47_out, or_13_out, jk_ff_2_q);
  and and_48 (and_48_out, and_45_out, or_13_out);
  not not_8 (not_8_out, or_13_out);
  and and_49 (and_49_out, or_13_out, and_41_out);
  Director director_2 (.En(or_14_out), .Clk(nClk), .Dir(jk_ff_6_q), .Up(director_2_up), .Dn(director_2_dn));
  not not_9 (not_9_out, and_36_out);
  not not_10 (not_10_out, Clk);
  Counter16 counter16_2 (
    .nUp(not_9_out), .nDn(not_6_out), .In({16{1'b0}}), .nLd(1'b1), .Clr(Rst), .Out(counter16_2_out));  // open: nBO
  not not_11 (not_11_out, and_26_out);
  Delay delay_1 (.in(and_33_out), .out(delay_1_out));
  not not_12 (not_12_out, delay_1_out);
  JK_FF jk_ff_5 (.J(and_47_out), .C(Clk), .K(and_44_out), .Q(jk_ff_5_q), .nQ(jk_ff_5_nq));
  JK_FF jk_ff_6 (.J(and_48_out), .C(not_10_out), .K(and_44_out), .Q(jk_ff_6_q));  // open: nQ
  Register #(.Bits(16)) register_1 (.D(counter16_1_out), .C(nClk), .en(and_49_out), .Q(register_1_q));
  Counter16 counter16_3 (
    .nUp(director_2_up), .nDn(director_2_dn), .In({16{1'b0}}), .nLd(1'b1), .Clr(Rst), .Out(ProgAddr));  // open: nBO
  // Probe on counter16_2_out
  RAMDualPort #(.AddrBits(16), .Bits(8)) Data (
    .A(counter16_2_out), .Din(driver_1_out), .str(or_10_out), .C(Clk), .ld(1'b1), .D(Data_d));
  not not_13 (not_13_out, and_27_out);
  and and_50 (and_50_out, jk_ff_5_q, jk_ff_3_q);
  // Probe on register_1_q
  Comparator #(.Bits(16)) comparator_2 (.a(register_1_q), .b(counter16_1_out), .eq(comparator_2_eq));  // open: gt, lt
  // Probe on counter16_1_out
  not not_14 (not_14_out, and_38_out);
  and and_51 (and_51_out, and_33_out, not_12_out);
  LED led_27 (.in(jk_ff_5_q));
  LED led_28 (.in(jk_ff_6_q));
  // Probe on ProgAddr
  // Probe on Data_d
  assign driver_1_out = and_39_out ? Data_d : 8'bz;  // Driver driver_1
  assign driver_1_out = and_31_out ? counter8_1_out : 8'bz;  // Driver driver_2
  assign driver_1_out = and_32_out ? Input : 8'bz;  // Driver driver_3
  RS_FF_AS rs_ff_as_1 (.S(and_51_out), .R(Send_out), .nQ(Proceed));  // open: Q
  Register #(.Bits(8)) register_2 (.D(driver_1_out), .C(Clk), .en(and_34_out), .Q(Output));
  Counter8 counter8_1 (
    .nUp(not_11_out), .nDn(not_13_out), .In(driver_1_out), .nLd(not_14_out), .Clr(Rst), .Out(counter8_1_out));  // open: nBO
  // Probe on counter8_1_out
  Button Send (.out(Send_out));
  LED led_29 (.in(and_34_out));

  // Notes on the sheet:
  //   _10Hz: Hz: 10
  //   BallsToTheWall: Hz: 2147483647
  //   Clock Select
  //   + -
  //   , .
  //   < >
  //   [ ]
  //   rom_1 loads program.bf
  //   +
  //   -
  //   ,
  //   .
  //   <
  //   >
  //   [
  //   ]
  //   Counter_Inc
  //   Pointer_Inc
  //   Pointer_Dec
  //   Data_In
  //   Data_Out
  //   Changer_Add
  //   Changer_Sub
  //   Changer_In
  //   Changer_Out
  //   Input_Out
  //   Input_Await
  //   Output_In
  //   Step_Rst
  //   Should Trigger
  //   Depth
  //   Pointer
  //   Counter
  //   Target Depth
  //   Current Depth
  //   Seek
  //   Dir
endmodule
